# Fritzing sketch autowater (saved by Fritzing 0.9.3b)
breadboards: 1

parts:
  부품1 = Arduino Uno (Rev3)
  부품2 = Soil Moisture Sensor
  Q1 = PNP-Transistor [package="TO92 [THT]"]
  R1 = Resistor [tolerance=±5% resistance=330 package=THT]
  M1 = DC Motor
  D1 = Rectifier Diode [part_number=1N4001 package="300 mil [THT]"]

nets:
  N1: 부품1.A0, 부품2.SIG
  N2: 부품1.D9_PWM, R1.Pin_0
  5V: 부품1.5V, 부품2.VCC, M1.pin_1, D1.anode
  GND: 부품1.GND, 부품2.GND, Q1.C
  N3: Q1.E, M1.pin_2, D1.cathode
  N4: Q1.B, R1.Pin_1

notes:
  [물 펌프]

// code stored in the sketch: autowater.ino
/*
 * Arduino auto watering system
 * 
 * Author : SeongKwon Choi <zerglinggo@zerglinggo.net>
 * License : MIT License
 */
int pinMoistureSensor = A0;
int pinWaterPump      = 9;
bool isSprinkle = false;
/*
 * soil moisture sensor value
 * Range : 0 ~ 1000
 * 
 * dry : 0 ~ 300
 * humid : 301 ~ 700
 * water : 701 ~ 1000
 */
int moistureLow  = 250;
int moistureHigh = 400

void setup() {
  // put your setup code here, to run once:
  Serial.begin(9600);
  pinMode(pinWaterPump, OUTPUT);
  digitalWrite(pinWaterPump, LOW);
}

void loop() {
  // put your main code here, to run repeatedly:
  int moistureValue;
  moistureValue = analogRead(pinMoistureSensor);
  Serial.println(moistureValue);
  
  if(isSprinkle) {
    digitalWrite(pinWaterPump, HIGH);
  } else {
    digitalWrite(pinWaterPump, LOW);
  }
  
  if(moistureValue <= moistureLow) {
    isSprinkle = true;
  } else if (moistureValue >= moistureHigh) {
    isSprinkle = false;
  }
}
